// Logisim project OpenCPU.circ as structural Verilog: 5 circuits, main circuit FullAdder
module FullAdder (
  input  A,
  input  B,
  input  A1,
  input  B1,
  output Sum,
  output Carry
);

  HalfAdder HA1 (.A(A), .B(B), .A1(A1), .B1(B1), .Sum(Sum), .Carry(Carry));
endmodule

module HalfAdder (
  input  A,
  input  B,
  input  A1,
  input  B1,
  output Sum,
  output Carry
);

  xor xor_1 (Carry, A1, B1);
  and and_1 (Sum, A, B);
endmodule

module ALU (
  input  A,
  input  B,
  input  A1,
  input  B1,
  input  A2,
  input  B2,
  input  A3,
  input  B3,
  input  A4,
  input  B4,
  input  A5,
  input  B5,
  input  A6,
  input  B6,
  input  A7,
  input  B7,
  output R0,
  output R1,
  output R2,
  output R3
);

  wire ALU0_carry, ALU0_sum, ALU1_carry, ALU1_sum, ALU2_carry, ALU2_sum, ALU3_carry, ALU3_sum;

  FullAdder ALU0 (.A(A), .B(B), .A1(A1), .B1(B1), .Sum(ALU0_sum), .Carry(ALU0_carry));
  FullAdder ALU1 (.A(A2), .B(B2), .A1(A3), .B1(B3), .Sum(ALU1_sum), .Carry(ALU1_carry));
  FullAdder ALU2 (.A(A4), .B(B4), .A1(A5), .B1(B5), .Sum(ALU2_sum), .Carry(ALU2_carry));
  FullAdder ALU3 (.A(A6), .B(B6), .A1(A7), .B1(B7), .Sum(ALU3_sum), .Carry(ALU3_carry));
  Multiplexer multiplexer_1 (.in0(ALU0_sum), .in1(ALU0_carry), .out(R0), .sel(1'b1));
  Multiplexer multiplexer_2 (.in0(ALU1_sum), .in1(ALU1_carry), .out(R1), .sel(1'b1));
  Multiplexer multiplexer_3 (.in0(ALU2_sum), .in1(ALU2_carry), .out(R2), .sel(1'b1));
  Multiplexer multiplexer_4 (.in0(ALU3_sum), .in1(ALU3_carry), .out(R3), .sel(1'b1));
endmodule

module CPU (
  input  in_1,
  input  in_2,
  input  in_3,
  input  in_4,
  input  in_5,
  input  in_6,
  input  in_7,
  input  in_8,
  input  in_9,
  input  in_10,
  input  in_11,
  input  in_12,
  input  in_13,
  input  in_14,
  input  in_15,
  input  in_16
);

  wire button_1_out, clock_1_out, controlcircuit_1_outp;
  wire [3:0] alu_1_r0;

  ALU alu_1 (
    .A(in_1), .B(in_2), .A1(in_3), .B1(in_4), .A2(in_5), .B2(in_6), .A3(in_7), .B3(in_8), .A4(in_9),
    .B4(in_10), .A5(in_11), .B5(in_12), .A6(in_13), .B6(in_14), .A7(in_15), .B7(in_16), .R0(alu_1_r0[0]),
    .R1(alu_1_r0[1]), .R2(alu_1_r0[2]), .R3(alu_1_r0[3]));
  ControlCircuit controlcircuit_1 (
    .R0(alu_1_r0[3]), .R1(alu_1_r0[2]), .R2(alu_1_r0[1]), .R3(alu_1_r0[0]), .outp(controlcircuit_1_outp));
  Register #(.width(4)) register_1 (
    .D(alu_1_r0), .en(controlcircuit_1_outp), .clk(clock_1_out), .clr(button_1_out));  // open: Q
  Clock clock_1 (.out(clock_1_out));
  Button button_1 (.out(button_1_out));
endmodule

module ControlCircuit (
  input  R0,
  input  R1,
  input  R2,
  input  R3,
  output outp
);

  or or_1 (outp, R0, R1, R2, R3);
endmodule
